# Fritzing sketch wireing (saved by Fritzing 0.9.3b)
circuit board: 11.5249cm x 10.8283cm

parts:
  Bauteil1 = Adafruit Feather 32u4 Bluefruit [part_number="Adafruit #2829"]
  NEOPIXEL1 = Neopixel Strip -- White (30/m)
  JACK1 = 2.1mm Barrel Jack with Terminal Block
  R1_(pull_up) = Resistor [tolerance=±5% resistance=10k package=THT]
  BUTTON1 = Arcade Button (green)
  NEOPIXEL2 = Neopixel Strip -- White (30/m)
  NEOPIXEL3 = Neopixel Strip -- White (30/m)
  NEOPIXEL4 = Neopixel Strip -- White (30/m)
  NEOPIXEL5 = Neopixel Strip -- White (30/m)
  NEOPIXEL6 = Neopixel Strip -- White (30/m)
  NEOPIXEL7 = Neopixel Strip -- White (30/m)
  C1 = Electrolytic Capacitor [capacitance=0.1mF package="100 mil [THT, electrolytic]"]

nets:
  N1: Bauteil1.GND, NEOPIXEL1.GND#1, JACK1.NEG, BUTTON1.no_name_yet#2, C1.-
  +5V: Bauteil1.VBUS, NEOPIXEL1.+5V, JACK1.POS, R1_(pull_up).Pin_0, NEOPIXEL2.+5V, NEOPIXEL3.+5V, NEOPIXEL4.+5V, NEOPIXEL5.+5V, NEOPIXEL6.+5V, NEOPIXEL7.+5V, C1.+
  N2: Bauteil1.10, R1_(pull_up).Pin_1, BUTTON1.no_name_yet#1
  N3: Bauteil1.6, NEOPIXEL1.Din
  N4: NEOPIXEL1.Dout, NEOPIXEL4.Din
  GND: NEOPIXEL1.GND#6, NEOPIXEL2.GND, NEOPIXEL3.GND, NEOPIXEL4.GND, NEOPIXEL5.GND, NEOPIXEL6.GND, NEOPIXEL7.GND
  N5: NEOPIXEL2.Din, NEOPIXEL7.Dout
  N6: NEOPIXEL3.Din, NEOPIXEL4.Dout
  N7: NEOPIXEL3.Dout, NEOPIXEL5.Din
  N8: NEOPIXEL5.Dout, NEOPIXEL6.Din
  N9: NEOPIXEL6.Dout, NEOPIXEL7.Din

custom parts:
  Adafruit Feather 32u4 Bluefruit: This is the Adafruit Feather 32u4 Bluefruit - our take on an 'all-in-one' Arduino-compatible + Bluetooth Low Energy with built in USB and battery charging. Its an Adafruit Feather 32u4 with a BTLE module, ready to rock! We have other boards in the Feather family, check'em out here. Bluetooth Low Energy is the hottest new low-power, 2.4GHz spectrum wireless protocol. In particular, its the only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
  Neopixel Strip -- White (30/m): These NeoPixel strips have 30 digitally-addressable pixel LEDs per meter and are very affordable and are only 12.5 mm wide, 10 mm if you remove the strip from the casing.
  Arcade Button (green): Adafruit Arcade Button (green)
